# Fritzing sketch L03_02_buttonLED (saved by Fritzing 1.0.4)
breadboards: 1

parts:
  A1 = Particle - Photon2
  R1 = Resistor [tolerance=±5% resistance=10 package="2010 [SMD]"]
  S1 = Pushbutton [package="[THT]"]
  LED1 = smd LED [color="Green (560nm)" package="0603 [SMD]"]
  R2 = Resistor [tolerance=±5% resistance=220 package="0603 [SMD]"]

nets (from the breadboard view):
  N1: A1.Pin_2, A1.Pin_31, S1.Pin_3, S1.Pin_4
  N2: A1.Pin_4, R1.Pin_1, R2.Pin_1
  N3: A1.Pin_20, R1.Pin_0, S1.Pin_1, S1.Pin_2
  N4: A1.Pin_23, A1.Pin_37, LED1.anode
  N5: LED1.cathode, R2.Pin_0

custom parts:
  Particle - Photon2: The Photon 2 is a microcontroller and Wi-Fi networking developed by particle. Features: 802.11a/b/g/n Wi-Fi, 2.4 GHz and 5 GHz Integrated PCB antenna Integrated U.FL connector for external antenna Integrated RF switch BLE 5 using same antenna as Wi-Fi Realtek RTL8721DM MCU ARM Cortex M33 CPU, 200 MHz 2048 KB (2 MB) user application maximum size 3072 KB (3 MB) of RAM available to user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
  Pushbutton: A generic pushbutton.
